# Fritzing sketch arduino_temp_motion_rf_sensor (saved by Fritzing 0.9.3b)
circuit board: 6.5cm x 6.5cm
breadboards: 1

parts:
  NRF24L01_Wireless_Transceiver = NRF24L01+ Breakout Board
  DHT22 = DHT22 Humidity and Temperature Sensor
  PIR = PIR sensor
  Green_LED_(activity) = LED - 3mm [color="Red (633nm)" package="3 mm [THT]"]
  Red_LED_(no_connection) = LED - 3mm [color="Red (633nm)" package="3 mm [THT]"]
  Arduino_Pro_Mini_5V = Arduino Pro Mini v13
  R_Green_LED = Resistor [tolerance=±5% resistance=330 package=THT]
  R_Red_LED = Resistor [tolerance=±5% resistance=330 package=THT]
  Voltage_Divider_1 = Resistor [tolerance=±5% resistance=220 package=THT]
  Voltage_Divider_2 = Resistor [tolerance=±5% resistance=330 package=THT]
  JP2 = Header 3 [package=jst-3-pth]
  R1 = Resistor [tolerance=±5% resistance=10k package=THT]

nets:
  GND: NRF24L01_Wireless_Transceiver.GND, DHT22.GND, PIR.GND, Green_LED_(activity).cathode, Red_LED_(no_connection).cathode, Arduino_Pro_Mini_5V.GND, Voltage_Divider_2.Pin_1, JP2.2
  N1: NRF24L01_Wireless_Transceiver.VCC, Voltage_Divider_1.Pin_0, Voltage_Divider_2.Pin_0
  N2: NRF24L01_Wireless_Transceiver.CE, Arduino_Pro_Mini_5V.D8
  N3: NRF24L01_Wireless_Transceiver.CS, Arduino_Pro_Mini_5V.D7
  N4: NRF24L01_Wireless_Transceiver.SCK, Arduino_Pro_Mini_5V.D13/SCK
  N5: NRF24L01_Wireless_Transceiver.MOSI, Arduino_Pro_Mini_5V.D11_PWM/MOSI
  N6: NRF24L01_Wireless_Transceiver.MISO, Arduino_Pro_Mini_5V.D12/MISO
  N7: NRF24L01_Wireless_Transceiver.IRQ, Arduino_Pro_Mini_5V.D3_PWM
  VDD: DHT22.VDD, PIR.VDD, Arduino_Pro_Mini_5V.VCC, Voltage_Divider_1.Pin_1, R1.Pin_1
  N8: DHT22.DATA, Arduino_Pro_Mini_5V.D6_PWM, R1.Pin_0
  N9: PIR.SIG, Arduino_Pro_Mini_5V.D2
  N10: Green_LED_(activity).anode, R_Green_LED.Pin_1
  N11: Red_LED_(no_connection).anode, R_Red_LED.Pin_1
  N12: Arduino_Pro_Mini_5V.RAW, JP2.1
  N13: Arduino_Pro_Mini_5V.D5_PWM, R_Red_LED.Pin_0
  N14: Arduino_Pro_Mini_5V.D4, R_Green_LED.Pin_0

custom parts:
  Arduino Pro Mini v13: It's blue! It's thin! It's the Arduino Pro Mini! SparkFun's minimal design approach to Arduino. This is a 5V Arduino running the 16MHz bootloader. Arduino Pro Mini does not come with connectors populated so that you can solder in any connector or wire with any orientation you need. We recommend first time Arduino users start with the Uno R3. It's a great board that will get you up and running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
